# Fritzing sketch acuan_logika (saved by Fritzing 0.9.3b)

parts:
  U1 = ESP32: sinyal terpakai
  U2 = DHT22 bare 4 pin
  R2 = R2 10000 ohm
  R1 = R1 220 ohm
  D1 = LED merah

nets:
  3V3: U1.3V3, U2.VCC, R2.1
  N1: U1.D15, U2.SDA, R2.2
  N2: U1.D23, R1.1
  N3: U1.GND.1, U2.GND, D1.C
  N4: R1.2, D1.A

custom parts:
  ESP32: sinyal terpakai: Simbol fungsional untuk menelusuri net. Bukan model fisik atau footprint PCB.
  DHT22 bare 4 pin: Simbol fungsional untuk menelusuri net. Bukan model fisik atau footprint PCB.
  R2 10000 ohm: Simbol fungsional untuk menelusuri net. Bukan model fisik atau footprint PCB.
  R1 220 ohm: Simbol fungsional untuk menelusuri net. Bukan model fisik atau footprint PCB.
  LED merah: Simbol fungsional untuk menelusuri net. Bukan model fisik atau footprint PCB.
